# Fritzing sketch microgroove-circuit (saved by Fritzing 1.0.1rc)
circuit board: 18.4009cm x 10.8561cm
breadboards: 2

parts:
  Pico_H1 = Raspberry Pi Pico H
  Part1 = OLED Monochrome 128x64 1.3 inch [part_number=938]
  RE1 = Rotary Encoder [package=THT]
  RE2 = Rotary Encoder [package=THT]
  RE3 = Rotary Encoder [package=THT]
  RE4 = Rotary Encoder [package=THT]
  RE5 = Rotary Encoder [package=THT]
  RE6 = Rotary Encoder [package=THT]
  IC1 = IC, DIP package, 6 pins [chip_label=H11L1 part_number=H11L1]
  D2 = Rectifier Diode [part_number=1N914 package="300 mil [THT]"]
  R1 = Resistor [tolerance=±5% power=0.25 resistance=220 package=THT]
  R2 = Resistor [tolerance=±5% power=0.25 resistance=470 package=THT]
  R3 = Resistor [tolerance=±5% power=0.25 resistance=33 package=THT]
  R4 = Resistor [tolerance=±5% power=0.25 resistance=10 package=THT]
  MIDI_in = Audio Jack (TRS) 3.5mm [package="PG203J [THT]"]
  MIDI_out = Audio Jack (TRS) 3.5mm [package="PG203J [THT]"]
  S1 = Pushbutton [package="[THT]"]
  S2 = Pushbutton [package="[THT]"]
  S3 = Pushbutton [package="[THT]"]

nets (from the pcb view):
  GND: Pico_H1.GND, Part1.GND, RE1.EncoderPinC, RE4.EncoderPinC, IC1.pin5, MIDI_in.Sleeve, MIDI_out.Sleeve
  3V3: Pico_H1.3V3, Part1.VIN, IC1.pin6, R2.Pin_0
  N1: Pico_H1.GP27_A1, Part1.SCLK_SCK
  N2: Pico_H1.GP26_A0, Part1.MOSI_SDA
  N3: Pico_H1.GP17, IC1.pin4, R2.Pin_1
  N4: Pico_H1.GP16, R3.Pin_1
  N5: Pico_H1.GP13, RE6.EncoderPinA
  N6: Pico_H1.GP12, RE5.EncoderPinB
  N7: Pico_H1.GP11, RE5.EncoderPinA
  N8: Pico_H1.GP10, RE4.EncoderPinB
  N9: Pico_H1.GP9, RE4.EncoderPinA
  N10: Pico_H1.GP8, RE3.EncoderPinB
  N11: Pico_H1.GP6, RE2.EncoderPinB
  N12: Pico_H1.GP5, RE2.EncoderPinA
  N13: Pico_H1.GP3, RE1.EncoderPinA
  N14: RE5.EncoderPinC, RE6.EncoderPinC
  N15: IC1.pin1, D2.cathode, R1.Pin_0
  N16: IC1.pin2, D2.anode, MIDI_in.Tip
  N17: R1.Pin_1, MIDI_in.Ring
  N18: R3.Pin_0, MIDI_out.Ring
  N19: R4.Pin_0, MIDI_out.Tip
  N20: S1.Pin_1, S1.Pin_2
  N21: S1.Pin_3, S1.Pin_4
  N22: S2.Pin_1, S2.Pin_2
  N23: S2.Pin_3, S2.Pin_4
  N24: S3.Pin_1, S3.Pin_2
  N25: S3.Pin_3, S3.Pin_4

notes:
  Encoders 1-3
  Encoders 4-6
  MIDI in
  MIDI out
  Adafruit OLED (mine is STEMMA, regular wiring shown here - YMMV)

custom parts:
  Raspberry Pi Pico H: Raspberry Pi Pico H. Based around the RP2040 microcontroller the Pico H is a low cost microcontroller device bringing Raspberry Pi quality, cost, and easy of use to the microcontroller space.
  OLED Monochrome 128x64 1.3 inch: These displays are small, only about 1.3" diagonal, but very readable due to the high contrast of an OLED display. This display is made of 128x64 individual white OLED pixels, each one is turned on or off by the controller chip. Because the display makes its own light, no backlight is required. This reduces the power required to run the OLED and is why the display has such high contrast; we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
